# Fritzing sketch led_push_button (saved by Fritzing 0.7.10b)
breadboards: 1

parts:
  R1 = Resistor [tolerance=±5% resistance=10k package=THT]
  S1 = Pushbutton [package="[THT]"]
  LED1 = LED - 5mm [color="White (8000K)" package="5 mm [THT]"]
  Arduino1 = Arduino
  Q1 = NPN-Transistor [package="TO92 [THT]"]
  LED4 = LED - 5mm [color="White (8000K)" package="5 mm [THT]"]
  LED5 = LED - 5mm [color="White (8000K)" package="5 mm [THT]"]
  LED6 = LED - 5mm [color="White (8000K)" package="5 mm [THT]"]
  R3 = Resistor [tolerance=±5% resistance=220 package=THT]
  R4 = Resistor [tolerance=±5% resistance=220 package=THT]
  R5 = Resistor [tolerance=±5% resistance=220 package=THT]
  R6 = Resistor [tolerance=±5% resistance=220 package=THT]
  R7 = Resistor [tolerance=±5% resistance=1k package=THT]

nets (from the breadboard view):
  N1: R1.Pin_0, Arduino1.GND, Q1.E
  N2: R1.Pin_1, S1.Pin_3, S1.Pin_4, Arduino1.D7
  N3: S1.Pin_1, S1.Pin_2, Arduino1.+5V, R3.Pin_1, R4.Pin_1, R5.Pin_1, R6.Pin_1
  N4: LED1.cathode, Q1.C, LED4.cathode, LED5.cathode, LED6.cathode
  N5: LED1.anode, R6.Pin_0
  N6: Arduino1.D9, R7.Pin_1
  N7: Q1.B, R7.Pin_0
  N8: LED4.anode, R5.Pin_0
  N9: LED5.anode, R4.Pin_0
  N10: LED6.anode, R3.Pin_0
